# Fritzing sketch Wiring_Schematics (saved by Fritzing 0.9.3b)
breadboards: 2

parts:
  Teensy1 = Teensy 3.6 (Basic)
  Raspberry_Pi_1 = Raspberry Pi 3 [part_number=RPI-3-V1.2]
  Part1 = 1.27 inch 16-bit Color OLED w microSD holder [part_number=1673]
  Part2 = 16-Channel 12-bit PWM Servo Driver - I2C [part_number=815]
  R1 = Resistor [tolerance=±5% resistance=4.7k package="0805 [SMD]"]
  R2 = Resistor [tolerance=±5% resistance=4.7k package="0805 [SMD]"]
  J2 = Basic Servo
  Part3 = 1.27 inch 16-bit Color OLED w microSD holder [part_number=1673]
  Part4 = 1.27 inch 16-bit Color OLED w microSD holder [part_number=1673]

nets:
  GND: Teensy1.GND, Teensy1.GND1, Raspberry_Pi_1.GND, Part1.GND, Part2.GND, J2.gnd, Part3.GND, Part4.GND
  N1: Teensy1.D0, Raspberry_Pi_1.GPIO14
  N2: Teensy1.D1, Raspberry_Pi_1.GPIO15
  N3: Teensy1.D11, Part1.MOSI
  N4: Teensy1.D13, Part1.CLK
  N5: Teensy1.A2/D16, Part1.DC
  N6: Teensy1.A3/D17, Part1.RESET
  N7: Teensy1.A4/D18, Part2.SDA, R1.Pin_1
  N8: Teensy1.A5/D19, Part2.SCL, R2.Pin_1
  N9: Teensy1.A8/D22, Part1.OLEDCS
  3V3: Teensy1.3V3, Teensy1.3V3_1, Part1.VIN, Part2.VCC, R1.Pin_0, R2.Pin_0
  VIN: Raspberry_Pi_1.3v3, Part3.VIN, Part4.VIN
  N10: Raspberry_Pi_1.GPIO9, Part3.MOSI, Part4.MOSI
  N11: Raspberry_Pi_1.GPIO11, Part3.CLK, Part4.CLK
  N12: Raspberry_Pi_1.GPIO5, Part3.RESET
  N13: Raspberry_Pi_1.GPIO6, Part4.RESET
  N14: Raspberry_Pi_1.GPIO7, Part4.OLEDCS
  N15: Raspberry_Pi_1.GPIO8, Part3.OLEDCS
  N16: Raspberry_Pi_1.GPIO24, Part3.DC
  N17: Raspberry_Pi_1.GPIO23, Part4.DC
  N18: Part2.PWM0, J2.pulse
  N19: Part2.5.0V, J2.vcc

notes:
  3.3V Power Input
  Servo Layout it up to you. I can change easily in software.
  Power GND

custom parts:
  Teensy 3.6 (Basic): The Teensy is a complete USB-based microcontoller development system, in a very small footprint, capable of implementing many types of projects. All programming is done via the USB port. No special programmer is needed, only a standard micro-USB cable and a PC or Macintosh with a USB port.
  1.27 inch 16-bit Color OLED w microSD holder: Our 1.27" color OLED displays are perfect when you need a small display with vivid, high-contrast 16-bit color. The visible portion of the OLED measures 1.27" diagonal and contains 128x96 RGB pixels, each one made of red, green and blue OLEDs. Each pixel can be set with 16-bits of resolution for a large range of colors. Because the display uses OLEDs, there is no backlight, and the contrast is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
  16-Channel 12-bit PWM Servo Driver - I2C: You want to make a cool robot, maybe a hexapod walker, or maybe just a piece of art with a lot of moving parts. Or maybe you want to drive a lot of LEDs with precise PWM output. Using only two pins, control 16 free-running PWM outputs! You can even chain up 62 breakouts to control up to 992 PWM outputs.
